// Logisim project cpu.circ as structural Verilog: 18 circuits, main circuit 1-bit-full-adder
module main (
  output [3:0] out_1,
  output out_2
);

  wire CLOCK_out, register_1_q0, register_1_q1, register_1_q2, register_1_q3, register_2_q0, register_2_q1,
       register_2_q2, register_2_q3;

  Clock CLOCK (.out(CLOCK_out));
  register register_1 (
    .c(CLOCK_out), .d0(1'b0), .d1(1'b0), .d2(1'b1), .d3(1'b0), .q0(register_1_q0), .q1(register_1_q1),
    .q2(register_1_q2), .q3(register_1_q3));
  register register_2 (
    .c(CLOCK_out), .d0(1'b0), .d1(1'b1), .d2(1'b0), .d3(1'b0), .q0(register_2_q0), .q1(register_2_q1),
    .q2(register_2_q2), .q3(register_2_q3));
  instr instr_1 ();  // open: c, e, b, f, a, g, h, i, j
  // _4_bit_add_sub 4_bit_add_sub_1: pin names not known; wires that end beside it: out_1

  // Notes on the sheet:
  //   REG1
  //   REG2
  //   SUB/ADD
endmodule

module _1_bit_full_adder (
  input  A,
  input  B,
  input  Cin,
  output S,
  output Cout
);

  wire and_1_out, and_2_out, xor_1_out;

  xor xor_1 (xor_1_out, A, B);
  and and_1 (and_1_out, A, B);
  xor xor_2 (S, xor_1_out, Cin);
  and and_2 (and_2_out, xor_1_out, Cin);
  or or_1 (Cout, and_2_out, and_1_out);
endmodule

module _4_bit_add_sub (
  input  A3,
  input  A2,
  input  A1,
  input  A0,
  input  D,
  input  B3,
  input  B2,
  input  B1,
  input  B0,
  output C,
  output S3,
  output S3_2,
  output S1,
  output S0
);

  wire n1_bit_full_adder_2_cout, n1_bit_full_adder_3_cout, n1_bit_full_adder_4_cout, xor_1_out, xor_2_out,
       xor_3_out, xor_4_out;

  xor xor_1 (xor_1_out, B3, D);
  xor xor_2 (xor_2_out, B2, D);
  _1_bit_full_adder u_1_bit_full_adder_1 (.A(A3), .B(xor_1_out), .S(S3), .Cin(n1_bit_full_adder_3_cout), .Cout(C));
  xor xor_3 (xor_3_out, B1, D);
  _1_bit_full_adder u_1_bit_full_adder_2 (
    .A(A1), .B(xor_3_out), .S(S1), .Cin(n1_bit_full_adder_4_cout), .Cout(n1_bit_full_adder_2_cout));
  _1_bit_full_adder u_1_bit_full_adder_3 (
    .A(A2), .B(xor_2_out), .S(S3_2), .Cin(n1_bit_full_adder_2_cout), .Cout(n1_bit_full_adder_3_cout));
  xor xor_4 (xor_4_out, B0, D);
  _1_bit_full_adder u_1_bit_full_adder_4 (.A(A0), .B(xor_4_out), .S(S0), .Cin(D), .Cout(n1_bit_full_adder_4_cout));
endmodule

module flipflop (
  input  D,
  input  C,
  output Q
);

  wire nand_1_out, nand_2_out, nor_2_out, not_1_out;

  not not_1 (not_1_out, D);
  nand nand_1 (nand_1_out, D, C);
  nand nand_2 (nand_2_out, C, not_1_out);
  nor nor_1 (Q, nand_1_out, nor_2_out);
  nor nor_2 (nor_2_out, Q, nand_2_out);

  // Notes on the sheet:
  //   set
  //   clock
  //   out
endmodule

module register (
  input  c,
  input  d0,
  input  d1,
  input  d2,
  input  d3,
  output q0,
  output q1,
  output q2,
  output q3
);

  flipflop flipflop_1 (.D(d0), .C(c), .Q(q0));
  flipflop flipflop_2 (.D(d1), .C(c), .Q(q1));
  flipflop flipflop_3 (.D(d2), .C(c), .Q(q2));
  flipflop flipflop_4 (.D(d3), .C(c), .Q(q3));
endmodule

module _2_bit_mul (
  input  A0,
  input  A1,
  input  B0,
  input  B1,
  output out_5,
  output out_6,
  output out_7,
  output out_8
);

  wire and_1_out, and_3_out, and_4_out, and_5_out;

  and and_1 (and_1_out, A0, B1);
  and and_2 (out_5, A0, B0);
  and and_3 (and_3_out, A1, B0);
  and and_4 (and_4_out, A1, B1);
  xor xor_1 (out_6, and_1_out, and_3_out);
  and and_5 (and_5_out, and_1_out, and_3_out);
  xor xor_2 (out_7, and_5_out, and_4_out);
  and and_6 (out_8, and_5_out, and_4_out);
endmodule

module MFPA (
  input  Ai,
  input  Bi,
  input  Ci,
  output Si,
  output nGi,
  output Pi
);

  xor xor_1 (Si, Pi, Ci);
  xor xor_2 (Pi, Ai, Bi);
  nand nand_1 (nGi, Ai, Bi);
endmodule

module MCLA_4 (
  input  B2,
  input  A2,
  input  B1,
  input  A1,
  input  B0,
  input  A0,
  input  C0,
  input  B3,
  input  A3,
  output S1,
  output S0,
  output S2,
  output S3,
  output P,
  output G
);

  wire mfpa_1_ngi, mfpa_1_pi, mfpa_2_ngi, mfpa_2_pi, mfpa_3_ngi, mfpa_4_ngi, mfpa_4_pi, nand_3_out,
       nand_4_out, nand_5_out, nand_6_out, nand_7_out, nand_8_out, nand_9_out, nand_10_out, nand_11_out,
       nand_12_out, nand_13_out, nand_14_out, not_1_out, not_2_out;

  nand nand_1 (G, mfpa_1_ngi, nand_3_out, nand_4_out, nand_5_out);
  MFPA mfpa_1 (.Ai(B3), .Bi(A3), .Si(S3), .nGi(mfpa_1_ngi), .Pi(mfpa_1_pi), .Ci(nand_6_out));
  nand nand_2 (P, mfpa_1_pi, mfpa_2_pi, C0, mfpa_4_pi);
  nand nand_3 (nand_3_out, mfpa_1_pi, not_1_out);
  nand nand_4 (nand_4_out, mfpa_1_pi, mfpa_2_pi, not_2_out);
  nand nand_5 (nand_5_out, mfpa_1_pi, mfpa_2_pi, C0, C0);
  nand nand_6 (nand_6_out, mfpa_2_ngi, nand_7_out, nand_8_out, nand_9_out);
  nand nand_7 (nand_7_out, mfpa_2_pi, C0);
  nand nand_8 (nand_8_out, mfpa_2_pi, C0, C0);
  nand nand_9 (nand_9_out, mfpa_2_pi, C0, mfpa_4_pi, C0);
  MFPA mfpa_2 (.Ai(B2), .Bi(A2), .Si(S2), .nGi(mfpa_2_ngi), .Pi(mfpa_2_pi), .Ci(nand_10_out));
  not not_1 (not_1_out, mfpa_2_ngi);
  nand nand_10 (nand_10_out, mfpa_3_ngi, nand_11_out, nand_12_out);
  nand nand_11 (nand_11_out, C0, mfpa_4_pi);
  nand nand_12 (nand_12_out, C0, mfpa_4_pi, C0);
  MFPA mfpa_3 (.Ai(B1), .Bi(A1), .Si(S1), .nGi(mfpa_3_ngi), .Pi(C0), .Ci(nand_13_out));
  not not_2 (not_2_out, mfpa_3_ngi);
  nand nand_13 (nand_13_out, mfpa_4_ngi, nand_14_out);
  nand nand_14 (nand_14_out, mfpa_4_pi, C0);
  MFPA mfpa_4 (.Ai(B0), .Bi(A0), .Si(S0), .nGi(mfpa_4_ngi), .Pi(mfpa_4_pi), .Ci(C0));
  not not_3 (C0, mfpa_4_ngi);
endmodule

module _4_bit_not (
  input  in_1,
  input  in_2,
  input  in_3,
  input  in_4,
  output out_5,
  output out_6,
  output out_7,
  output out_8
);

  not not_1 (out_5, in_1);
  not not_2 (out_6, in_2);
  not not_3 (out_7, in_3);
  not not_4 (out_8, in_4);
endmodule

module alu (
  input  SEL0,
  input  SEL1,
  input  SEL1_2,
  input  A0,
  input  A1,
  input  A2,
  input  A3,
  input  B0,
  input  B1,
  input  B2,
  input  B3,
  output OUT0,
  output OUT1,
  output OUT3,
  output OUT4,
  output CARRY
);

  wire controlled_buffer_1_out, controlled_buffer_2_out, controlled_buffer_3_out, controlled_buffer_4_out,
       instr_1_p4;

  // instr instr_1: pin names not known; wires that end beside it: SEL0, SEL1, SEL1_2, instr_1_p4
  assign controlled_buffer_1_out = instr_1_p4 ? A0 : 1'bz;  // Controlled_Buffer controlled_buffer_1
  assign controlled_buffer_2_out = instr_1_p4 ? A1 : 1'bz;  // Controlled_Buffer controlled_buffer_2
  assign controlled_buffer_3_out = instr_1_p4 ? A2 : 1'bz;  // Controlled_Buffer controlled_buffer_3
  assign controlled_buffer_4_out = instr_1_p4 ? A3 : 1'bz;  // Controlled_Buffer controlled_buffer_4
  _4_bit_add_sub ADD_SUB (
    .A3(OUT1), .A2(OUT3), .A1(OUT4), .S3_2(OUT0), .S1(OUT1), .S0(OUT3));  // open: C, B3, B2, B1, B0, A0, D, S3
  _4_bit_rol ROL (.B0(OUT0), .B1(OUT1), .B2(OUT3), .B3(OUT4));  // open: A0, A1, A2, A3
  _4_bit_ror ROR (.B0(OUT0), .B1(OUT1), .B2(OUT3), .B3(OUT4));  // open: A0, A1, A2, A3
  _4_bit_shl SHL (.out_5(OUT0), .out_6(OUT1), .out_7(OUT3), .out_8(OUT4));  // open: in_1, in_2, in_3, in_4
  _4_bit_shr SHR (
    .in_1(controlled_buffer_1_out), .in_2(controlled_buffer_2_out), .in_3(controlled_buffer_3_out),
    .in_4(controlled_buffer_4_out), .out_5(OUT0), .out_6(OUT1), .out_7(OUT3), .out_8(OUT4));
endmodule

module _4_bit_rol (
  input  A0,
  input  A1,
  input  A2,
  input  A3,
  output B0,
  output B1,
  output B2,
  output B3
);


  assign B0 = A3;
  assign B1 = A0;
  assign B2 = A1;
  assign B3 = A2;
endmodule

module _4_bit_ror (
  input  A0,
  input  A1,
  input  A2,
  input  A3,
  output B0,
  output B1,
  output B2,
  output B3
);


  assign B0 = A1;
  assign B1 = A2;
  assign B2 = A3;
  assign B3 = A0;
endmodule

module _4_bit_shl (
  input  in_1,
  input  in_2,
  input  in_3,
  input  in_4,
  output out_5,
  output out_6,
  output out_7,
  output out_8
);

  _4_bit_rol u_4_bit_rol_1 (
    .A0(in_1), .A1(in_2), .A2(in_3), .A3(in_4), .B1(out_6), .B2(out_7), .B3(out_8));  // open: B0
endmodule

module _4_bit_shr (
  input  in_1,
  input  in_2,
  input  in_3,
  input  in_4,
  output out_5,
  output out_6,
  output out_7,
  output out_8
);

  _4_bit_ror u_4_bit_ror_1 (
    .A0(in_1), .A1(in_2), .A2(in_3), .A3(in_4), .B0(out_5), .B1(out_6), .B2(out_7));  // open: B3
endmodule

module instr (
  input  c,
  input  b,
  input  a,
  output e,
  output f,
  output g,
  output h,
  output i,
  output j
);

  wire and_1_out, and_2_out, and_3_out, and_4_out, and_5_out, and_6_out, not_1_out, not_2_out, not_3_out,
       not_4_out, not_5_out, not_6_out, not_7_out, not_8_out, not_9_out;

  not not_1 (not_1_out, c);
  not not_2 (not_2_out, b);
  not not_3 (not_3_out, c);
  not not_4 (not_4_out, c);
  not not_5 (not_5_out, b);
  not not_6 (not_6_out, b);
  and and_1 (and_1_out, c, b);
  not not_7 (not_7_out, a);
  and and_2 (and_2_out, not_1_out, not_2_out);
  and and_3 (and_3_out, not_3_out, b);
  not not_8 (not_8_out, a);
  and and_4 (and_4_out, not_4_out, b);
  and and_5 (and_5_out, c, not_5_out);
  not not_9 (not_9_out, a);
  and and_6 (and_6_out, c, not_6_out);
  and and_7 (j, and_1_out, not_7_out);
  and and_8 (e, and_2_out, a);
  and and_9 (f, and_3_out, not_8_out);
  and and_10 (g, and_4_out, a);
  and and_11 (h, and_5_out, not_9_out);
  and and_12 (i, and_6_out, a);
endmodule

module ALU (
  input  A0,
  input  A1,
  input  A2,
  input  A3,
  input  B0,
  input  B1,
  input  B2,
  input  B3,
  input  I0,
  input  I1,
  input  I2,
  output D0,
  output D1,
  output D2,
  output D3,
  output C
);

  wire controlled_buffer_1_out, controlled_buffer_2_out, controlled_buffer_3_out, controlled_buffer_4_out,
       controlled_buffer_5_out, controlled_buffer_6_out, controlled_buffer_11_out, controlled_buffer_12_out,
       controlled_buffer_13_out, controlled_buffer_14_out, controlled_buffer_16_out,
       controlled_buffer_17_out, controlled_buffer_18_out, controlled_buffer_19_out,
       controlled_buffer_20_out, controlled_buffer_21_out, controlled_inverter_1_out, instr_1_e, instr_1_f,
       instr_1_g, instr_1_h, instr_1_i, instr_1_j, n4_bit_add_sub_1_c, n4_bit_add_sub_1_s0,
       n4_bit_add_sub_1_s1, n4_bit_add_sub_1_s3, n4_bit_add_sub_1_s3_2, or_1_out;

  assign controlled_inverter_1_out = instr_1_e ? ~n4_bit_add_sub_1_c : 1'bz;  // Controlled_Inverter controlled_inverter_1
  instr instr_1 (
    .c(I2), .e(instr_1_e), .b(I1), .f(instr_1_f), .a(I0), .g(instr_1_g), .h(instr_1_h), .i(instr_1_i),
    .j(instr_1_j));
  or or_1 (or_1_out, instr_1_f, instr_1_e);
  assign controlled_buffer_1_out = or_1_out ? A0 : 1'bz;  // Controlled_Buffer controlled_buffer_1
  assign controlled_buffer_2_out = or_1_out ? A1 : 1'bz;  // Controlled_Buffer controlled_buffer_2
  _4_bit_add_sub u_4_bit_add_sub_1 (
    .C(n4_bit_add_sub_1_c), .B3(controlled_buffer_11_out), .B2(controlled_buffer_12_out),
    .B1(controlled_buffer_4_out), .B0(controlled_buffer_3_out), .A3(controlled_buffer_6_out),
    .A2(controlled_buffer_5_out), .A1(controlled_buffer_2_out), .A0(controlled_buffer_1_out), .D(instr_1_e),
    .S3(n4_bit_add_sub_1_s3), .S3_2(n4_bit_add_sub_1_s3_2), .S1(n4_bit_add_sub_1_s1), .S0(n4_bit_add_sub_1_s0));
  assign controlled_buffer_3_out = or_1_out ? B0 : 1'bz;  // Controlled_Buffer controlled_buffer_3
  assign controlled_buffer_4_out = or_1_out ? B1 : 1'bz;  // Controlled_Buffer controlled_buffer_4
  assign controlled_buffer_5_out = or_1_out ? A2 : 1'bz;  // Controlled_Buffer controlled_buffer_5
  assign controlled_buffer_6_out = or_1_out ? A3 : 1'bz;  // Controlled_Buffer controlled_buffer_6
  assign D2 = or_1_out ? n4_bit_add_sub_1_s3_2 : 1'bz;  // Controlled_Buffer controlled_buffer_7
  assign D3 = or_1_out ? n4_bit_add_sub_1_s3 : 1'bz;  // Controlled_Buffer controlled_buffer_8
  assign D0 = or_1_out ? n4_bit_add_sub_1_s0 : 1'bz;  // Controlled_Buffer controlled_buffer_9
  assign D1 = or_1_out ? n4_bit_add_sub_1_s1 : 1'bz;  // Controlled_Buffer controlled_buffer_10
  assign controlled_buffer_11_out = or_1_out ? B3 : 1'bz;  // Controlled_Buffer controlled_buffer_11
  assign controlled_buffer_12_out = or_1_out ? B2 : 1'bz;  // Controlled_Buffer controlled_buffer_12
  assign controlled_buffer_13_out = instr_1_g ? A3 : 1'bz;  // Controlled_Buffer controlled_buffer_13
  assign controlled_buffer_14_out = instr_1_g ? A2 : 1'bz;  // Controlled_Buffer controlled_buffer_14
  assign C = or_1_out ? controlled_inverter_1_out : 1'bz;  // Controlled_Buffer controlled_buffer_15
  assign controlled_buffer_16_out = instr_1_h ? A2 : 1'bz;  // Controlled_Buffer controlled_buffer_16
  assign controlled_buffer_17_out = instr_1_g ? A0 : 1'bz;  // Controlled_Buffer controlled_buffer_17
  assign controlled_buffer_18_out = instr_1_g ? A1 : 1'bz;  // Controlled_Buffer controlled_buffer_18
  assign controlled_buffer_19_out = instr_1_h ? A3 : 1'bz;  // Controlled_Buffer controlled_buffer_19
  _4_bit_rol u_4_bit_rol_1 (
    .A0(controlled_buffer_17_out), .A1(controlled_buffer_18_out), .A2(controlled_buffer_14_out),
    .A3(controlled_buffer_13_out), .B0(D0), .B1(D1), .B2(D2), .B3(D3));
  assign controlled_buffer_20_out = instr_1_h ? A1 : 1'bz;  // Controlled_Buffer controlled_buffer_20
  assign controlled_buffer_21_out = instr_1_h ? A0 : 1'bz;  // Controlled_Buffer controlled_buffer_21
  _4_bit_ror u_4_bit_ror_1 (
    .A0(controlled_buffer_21_out), .A1(controlled_buffer_20_out), .A2(controlled_buffer_16_out),
    .A3(controlled_buffer_19_out), .B0(D0), .B1(D1), .B2(D2), .B3(D3));
endmodule

module _4_bit_add_sublol (
  input  A3,
  input  A2,
  input  A1,
  input  A0,
  input  D,
  input  B3,
  input  B2,
  input  B1,
  input  B0,
  output C,
  output S3,
  output S32,
  output S1,
  output S0
);

  wire and_1_out, and_2_out, and_3_out, and_4_out, and_5_out, and_6_out, and_7_out, and_8_out, and_9_out,
       and_10_out, and_11_out, and_12_out, and_13_out, and_14_out, and_15_out, and_16_out, and_17_out,
       and_18_out, and_19_out, and_20_out, and_21_out, and_22_out, and_23_out, and_24_out, and_25_out,
       and_26_out, and_27_out, and_28_out, and_29_out, and_30_out, and_31_out, and_32_out, and_33_out,
       and_34_out, and_35_out, and_36_out, and_37_out, and_38_out, and_39_out, and_40_out, and_41_out,
       and_42_out, and_43_out, and_44_out, and_45_out, and_46_out, and_47_out, and_48_out, and_49_out,
       and_50_out, and_51_out, and_52_out, and_53_out, and_54_out, and_55_out, and_56_out, and_57_out,
       and_58_out, and_59_out, and_60_out, and_61_out, and_62_out, and_63_out, and_64_out, and_65_out,
       and_66_out, and_67_out, and_68_out, and_69_out, and_70_out, and_71_out, and_72_out, and_73_out,
       and_74_out, and_75_out, and_76_out, and_77_out, and_78_out, and_79_out, and_80_out, and_81_out,
       and_82_out, and_83_out, and_84_out, and_85_out, and_86_out, and_87_out, and_88_out, and_89_out,
       and_90_out, and_91_out, and_92_out, and_93_out, and_94_out, and_95_out, and_96_out, and_97_out,
       and_98_out, and_99_out, and_100_out, and_101_out, and_102_out, and_103_out, and_104_out, and_105_out,
       and_106_out, and_107_out, and_108_out, and_109_out, and_110_out, and_111_out, and_112_out,
       and_113_out, and_114_out, and_115_out, and_116_out, and_117_out, and_118_out, and_119_out,
       and_120_out, and_121_out, and_122_out, and_123_out, and_124_out, and_125_out, and_126_out,
       and_127_out, and_128_out, and_129_out, and_130_out, and_131_out, and_132_out, and_133_out,
       and_134_out, and_135_out, and_136_out, and_137_out, and_138_out, and_139_out, and_140_out,
       and_141_out, not_1_out, not_2_out, not_3_out, not_4_out, not_5_out, not_6_out, not_7_out, not_8_out,
       not_9_out, not_10_out, not_11_out, not_12_out, not_13_out, not_14_out, not_15_out, not_16_out,
       not_17_out, not_18_out, not_19_out, not_20_out, not_21_out, not_22_out, not_23_out, not_24_out,
       not_25_out, not_26_out, not_27_out, not_28_out, not_29_out, not_30_out, not_31_out, not_32_out,
       not_33_out, not_34_out, not_35_out, not_36_out, not_37_out, not_38_out, not_39_out, not_40_out,
       not_41_out, not_42_out, not_43_out, not_44_out, not_45_out, not_46_out, not_47_out, not_48_out,
       not_49_out, not_50_out, not_51_out, not_52_out, not_53_out, not_54_out, not_55_out, not_56_out,
       not_57_out, not_58_out, not_59_out, not_60_out, not_61_out, not_62_out, not_63_out, not_64_out,
       not_65_out, not_66_out, not_67_out, not_68_out, not_69_out, not_70_out, not_71_out, not_72_out,
       not_73_out, not_74_out, not_75_out, not_76_out, not_77_out, not_78_out, not_79_out, not_80_out,
       not_81_out, not_82_out, not_83_out, not_84_out, not_85_out, not_86_out, not_87_out, not_88_out,
       not_89_out, not_90_out, not_91_out, not_92_out, not_93_out, not_94_out, not_95_out, not_96_out,
       not_97_out, not_98_out, not_99_out, not_100_out, not_101_out, not_102_out, not_103_out, not_104_out,
       not_105_out, not_106_out, not_107_out, not_108_out, not_109_out, not_110_out, not_111_out,
       not_112_out, not_113_out, not_114_out, not_115_out, not_116_out, not_117_out, not_118_out,
       not_119_out, not_120_out, not_121_out, not_122_out, not_123_out, not_124_out, not_125_out,
       not_126_out, not_127_out, not_128_out, not_129_out, not_130_out, not_131_out, not_132_out,
       not_133_out, not_134_out, not_135_out, not_136_out, not_137_out, not_138_out, not_139_out,
       not_140_out, not_141_out, not_142_out, not_143_out, not_144_out, not_145_out, not_146_out,
       not_147_out, not_148_out, not_149_out, not_150_out, not_151_out, not_152_out, not_153_out,
       not_154_out, not_155_out, not_156_out, not_157_out, not_158_out, not_159_out, not_160_out,
       not_161_out, not_162_out, not_163_out, not_164_out, not_165_out, not_166_out, not_167_out,
       not_168_out, not_169_out, not_170_out, not_171_out, not_172_out, not_173_out, not_174_out,
       not_175_out, not_176_out, not_177_out, not_178_out, not_179_out, not_180_out, not_181_out,
       not_182_out, not_183_out, not_184_out, not_185_out, not_186_out, not_187_out, not_188_out,
       not_189_out, not_190_out, not_191_out, not_192_out, not_193_out, not_194_out, not_195_out,
       not_196_out, not_197_out, not_198_out, not_199_out, not_200_out, not_201_out, not_202_out,
       not_203_out, not_204_out, not_205_out, not_206_out, not_207_out, not_208_out, not_209_out,
       not_210_out, not_211_out, not_212_out, not_213_out, not_214_out, not_215_out, not_216_out,
       not_217_out, not_218_out, not_219_out, not_220_out, not_221_out, not_222_out, not_223_out,
       not_224_out, not_225_out, not_226_out, not_227_out, not_228_out, not_229_out, not_230_out,
       not_231_out, not_232_out, not_233_out, not_234_out, not_235_out, not_236_out, not_237_out,
       not_238_out, not_239_out, not_240_out, not_241_out, not_242_out, not_243_out, not_244_out,
       not_245_out, not_246_out, not_247_out, not_248_out, not_249_out, not_250_out, not_251_out,
       not_252_out, not_253_out, not_254_out, not_255_out, not_256_out, not_257_out, not_258_out,
       not_259_out, not_260_out, not_261_out, not_262_out, not_263_out, not_264_out, not_265_out,
       not_266_out, not_267_out, not_268_out, not_269_out, not_270_out, not_271_out, not_272_out,
       not_273_out, not_274_out, not_275_out, not_276_out, not_277_out, not_278_out, not_279_out,
       not_280_out, not_281_out, not_282_out, not_283_out, not_284_out, not_285_out, not_286_out,
       not_287_out, not_288_out, not_289_out, not_290_out, not_291_out, not_292_out, not_293_out,
       not_294_out, not_295_out, not_296_out, not_297_out, not_298_out, not_299_out, not_300_out,
       not_301_out, not_302_out, not_303_out, not_304_out, not_305_out, not_306_out, not_307_out,
       not_308_out, not_309_out, not_310_out, not_311_out, not_312_out, not_313_out, not_314_out,
       not_315_out, not_316_out, not_317_out, not_318_out, not_319_out, not_320_out, not_321_out,
       not_322_out, not_323_out, not_324_out, not_325_out, not_326_out, not_327_out, not_328_out,
       not_329_out, not_330_out, not_331_out, not_332_out, not_333_out, not_334_out, not_335_out,
       not_336_out, not_337_out, not_338_out, not_339_out, not_340_out, not_341_out, not_342_out,
       not_343_out, not_344_out, not_345_out, not_346_out, not_347_out, not_348_out, not_349_out,
       not_350_out, or_3_out, or_4_out, or_5_out, or_6_out, or_7_out;

  not not_1 (not_1_out, B3);
  not not_2 (not_2_out, B2);
  not not_3 (not_3_out, B1);
  not not_4 (not_4_out, B0);
  not not_5 (not_5_out, D);
  not not_6 (not_6_out, B3);
  not not_7 (not_7_out, B2);
  not not_8 (not_8_out, B1);
  not not_9 (not_9_out, D);
  not not_10 (not_10_out, B3);
  not not_11 (not_11_out, B2);
  not not_12 (not_12_out, B1);
  not not_13 (not_13_out, B3);
  not not_14 (not_14_out, B2);
  not not_15 (not_15_out, B0);
  not not_16 (not_16_out, D);
  not not_17 (not_17_out, B3);
  not not_18 (not_18_out, B2);
  not not_19 (not_19_out, D);
  not not_20 (not_20_out, B3);
  not not_21 (not_21_out, B2);
  not not_22 (not_22_out, B3);
  not not_23 (not_23_out, B1);
  not not_24 (not_24_out, B0);
  not not_25 (not_25_out, D);
  not not_26 (not_26_out, B3);
  not not_27 (not_27_out, B1);
  not not_28 (not_28_out, D);
  not not_29 (not_29_out, B3);
  not not_30 (not_30_out, B1);
  not not_31 (not_31_out, B3);
  not not_32 (not_32_out, B0);
  not not_33 (not_33_out, D);
  not not_34 (not_34_out, B3);
  not not_35 (not_35_out, D);
  not not_36 (not_36_out, B3);
  not not_37 (not_37_out, B2);
  not not_38 (not_38_out, B1);
  not not_39 (not_39_out, B0);
  not not_40 (not_40_out, D);
  not not_41 (not_41_out, B2);
  not not_42 (not_42_out, B1);
  not not_43 (not_43_out, B3);
  not not_44 (not_44_out, B2);
  not not_45 (not_45_out, B0);
  not not_46 (not_46_out, B2);
  not not_47 (not_47_out, B1);
  not not_48 (not_48_out, D);
  not not_49 (not_49_out, B2);
  not not_50 (not_50_out, D);
  not not_51 (not_51_out, B2);
  not not_52 (not_52_out, B1);
  not not_53 (not_53_out, B0);
  not not_54 (not_54_out, B3);
  not not_55 (not_55_out, B1);
  not not_56 (not_56_out, D);
  not not_57 (not_57_out, B0);
  not not_58 (not_58_out, B1);
  not not_59 (not_59_out, A3);
  not not_60 (not_60_out, A2);
  not not_61 (not_61_out, A1);
  not not_62 (not_62_out, A0);
  not not_63 (not_63_out, D);
  not not_64 (not_64_out, A3);
  not not_65 (not_65_out, A2);
  not not_66 (not_66_out, A1);
  not not_67 (not_67_out, D);
  not not_68 (not_68_out, B1);
  not not_69 (not_69_out, A3);
  not not_70 (not_70_out, A2);
  not not_71 (not_71_out, A1);
  not not_72 (not_72_out, D);
  not not_73 (not_73_out, B0);
  not not_74 (not_74_out, A3);
  not not_75 (not_75_out, A2);
  not not_76 (not_76_out, A0);
  not not_77 (not_77_out, D);
  not not_78 (not_78_out, B1);
  not not_79 (not_79_out, A3);
  not not_80 (not_80_out, A2);
  not not_81 (not_81_out, D);
  not not_82 (not_82_out, B2);
  not not_83 (not_83_out, A3);
  not not_84 (not_84_out, A2);
  not not_85 (not_85_out, D);
  not not_86 (not_86_out, B1);
  not not_87 (not_87_out, B0);
  not not_88 (not_88_out, A3);
  not not_89 (not_89_out, A1);
  not not_90 (not_90_out, D);
  not not_91 (not_91_out, B2);
  not not_92 (not_92_out, B0);
  not not_93 (not_93_out, A3);
  not not_94 (not_94_out, B2);
  not not_95 (not_95_out, B1);
  not not_96 (not_96_out, B0);
  not not_97 (not_97_out, A3);
  not not_98 (not_98_out, A2);
  not not_99 (not_99_out, A1);
  not not_100 (not_100_out, A0);
  not not_101 (not_101_out, B3);
  not not_102 (not_102_out, A3);
  not not_103 (not_103_out, A2);
  not not_104 (not_104_out, A1);
  not not_105 (not_105_out, B3);
  not not_106 (not_106_out, A3);
  not not_107 (not_107_out, A2);
  not not_108 (not_108_out, A0);
  not not_109 (not_109_out, B3);
  not not_110 (not_110_out, A3);
  not not_111 (not_111_out, A2);
  not not_112 (not_112_out, B3);
  not not_113 (not_113_out, A3);
  not not_114 (not_114_out, A1);
  not not_115 (not_115_out, A0);
  not not_116 (not_116_out, B3);
  not not_117 (not_117_out, A3);
  not not_118 (not_118_out, A0);
  not not_119 (not_119_out, B3);
  not not_120 (not_120_out, A3);
  not not_121 (not_121_out, A2);
  not not_122 (not_122_out, B3);
  not not_123 (not_123_out, A3);
  not not_124 (not_124_out, A1);
  not not_125 (not_125_out, B2);
  not not_126 (not_126_out, B1);
  not not_127 (not_127_out, A3);
  not not_128 (not_128_out, A2);
  not not_129 (not_129_out, B3);
  not not_130 (not_130_out, A3);
  not not_131 (not_131_out, A2);
  not not_132 (not_132_out, B2);
  not not_133 (not_133_out, B0);
  not not_134 (not_134_out, A3);
  not not_135 (not_135_out, A0);
  not not_136 (not_136_out, B2);
  not not_137 (not_137_out, B1);
  not not_138 (not_138_out, A3);
  not not_139 (not_139_out, A2);
  not not_140 (not_140_out, B3);
  not not_141 (not_141_out, A3);
  not not_142 (not_142_out, A2);
  not not_143 (not_143_out, B2);
  not not_144 (not_144_out, A3);
  not not_145 (not_145_out, D);
  not not_146 (not_146_out, B3);
  not not_147 (not_147_out, A3);
  not not_148 (not_148_out, A1);
  not not_149 (not_149_out, B3);
  not not_150 (not_150_out, A3);
  not not_151 (not_151_out, A1);
  not not_152 (not_152_out, A0);
  not not_153 (not_153_out, B2);
  not not_154 (not_154_out, A3);
  not not_155 (not_155_out, B2);
  not not_156 (not_156_out, A3);
  not not_157 (not_157_out, B1);
  not not_158 (not_158_out, B0);
  not not_159 (not_159_out, A3);
  not not_160 (not_160_out, D);
  not not_161 (not_161_out, B3);
  not not_162 (not_162_out, A3);
  not not_163 (not_163_out, B1);
  not not_164 (not_164_out, A3);
  not not_165 (not_165_out, D);
  not not_166 (not_166_out, B3);
  not not_167 (not_167_out, A3);
  not not_168 (not_168_out, B1);
  not not_169 (not_169_out, A3);
  not not_170 (not_170_out, B0);
  not not_171 (not_171_out, A3);
  not not_172 (not_172_out, D);
  not not_173 (not_173_out, B3);
  not not_174 (not_174_out, A3);
  not not_175 (not_175_out, A2);
  not not_176 (not_176_out, A1);
  not not_177 (not_177_out, A0);
  not not_178 (not_178_out, D);
  not not_179 (not_179_out, B3);
  not not_180 (not_180_out, A2);
  not not_181 (not_181_out, A1);
  not not_182 (not_182_out, D);
  not not_183 (not_183_out, B3);
  not not_184 (not_184_out, B1);
  not not_185 (not_185_out, A2);
  not not_186 (not_186_out, A1);
  not not_187 (not_187_out, D);
  not not_188 (not_188_out, B3);
  not not_189 (not_189_out, B0);
  not not_190 (not_190_out, A2);
  not not_191 (not_191_out, A0);
  not not_192 (not_192_out, D);
  not not_193 (not_193_out, B3);
  not not_194 (not_194_out, B1);
  not not_195 (not_195_out, A2);
  not not_196 (not_196_out, D);
  not not_197 (not_197_out, B3);
  not not_198 (not_198_out, B2);
  not not_199 (not_199_out, A2);
  not not_200 (not_200_out, D);
  not not_201 (not_201_out, B3);
  not not_202 (not_202_out, B1);
  not not_203 (not_203_out, B0);
  not not_204 (not_204_out, A1);
  not not_205 (not_205_out, A0);
  not not_206 (not_206_out, D);
  not not_207 (not_207_out, B3);
  not not_208 (not_208_out, B2);
  not not_209 (not_209_out, B3);
  not not_210 (not_210_out, B2);
  not not_211 (not_211_out, B1);
  not not_212 (not_212_out, B0);
  not not_213 (not_213_out, A2);
  not not_214 (not_214_out, A1);
  not not_215 (not_215_out, A0);
  not not_216 (not_216_out, A2);
  not not_217 (not_217_out, A1);
  not not_218 (not_218_out, A2);
  not not_219 (not_219_out, A0);
  not not_220 (not_220_out, A2);
  not not_221 (not_221_out, A1);
  not not_222 (not_222_out, A1);
  not not_223 (not_223_out, B3);
  not not_224 (not_224_out, B2);
  not not_225 (not_225_out, B1);
  not not_226 (not_226_out, A2);
  not not_227 (not_227_out, A2);
  not not_228 (not_228_out, B3);
  not not_229 (not_229_out, B2);
  not not_230 (not_230_out, B0);
  not not_231 (not_231_out, A0);
  not not_232 (not_232_out, B3);
  not not_233 (not_233_out, B2);
  not not_234 (not_234_out, B1);
  not not_235 (not_235_out, A2);
  not not_236 (not_236_out, A2);
  not not_237 (not_237_out, B3);
  not not_238 (not_238_out, B2);
  not not_239 (not_239_out, A2);
  not not_240 (not_240_out, A1);
  not not_241 (not_241_out, B3);
  not not_242 (not_242_out, B2);
  not not_243 (not_243_out, B0);
  not not_244 (not_244_out, D);
  not not_245 (not_245_out, A1);
  not not_246 (not_246_out, A0);
  not not_247 (not_247_out, A0);
  not not_248 (not_248_out, B3);
  not not_249 (not_249_out, B2);
  not not_250 (not_250_out, B3);
  not not_251 (not_251_out, B1);
  not not_252 (not_252_out, B0);
  not not_253 (not_253_out, D);
  not not_254 (not_254_out, B3);
  not not_255 (not_255_out, B1);
  not not_256 (not_256_out, D);
  not not_257 (not_257_out, B3);
  not not_258 (not_258_out, B1);
  not not_259 (not_259_out, B3);
  not not_260 (not_260_out, B0);
  not not_261 (not_261_out, D);
  not not_262 (not_262_out, B3);
  not not_263 (not_263_out, A2);
  not not_264 (not_264_out, A1);
  not not_265 (not_265_out, A0);
  not not_266 (not_266_out, D);
  not not_267 (not_267_out, A2);
  not not_268 (not_268_out, A1);
  not not_269 (not_269_out, D);
  not not_270 (not_270_out, B0);
  not not_271 (not_271_out, A2);
  not not_272 (not_272_out, B1);
  not not_273 (not_273_out, B0);
  not not_274 (not_274_out, A2);
  not not_275 (not_275_out, A1);
  not not_276 (not_276_out, A0);
  not not_277 (not_277_out, B2);
  not not_278 (not_278_out, A2);
  not not_279 (not_279_out, A1);
  not not_280 (not_280_out, B2);
  not not_281 (not_281_out, A2);
  not not_282 (not_282_out, A0);
  not not_283 (not_283_out, B2);
  not not_284 (not_284_out, A2);
  not not_285 (not_285_out, A1);
  not not_286 (not_286_out, B2);
  not not_287 (not_287_out, A2);
  not not_288 (not_288_out, A1);
  not not_289 (not_289_out, B1);
  not not_290 (not_290_out, A2);
  not not_291 (not_291_out, D);
  not not_292 (not_292_out, B2);
  not not_293 (not_293_out, A2);
  not not_294 (not_294_out, A0);
  not not_295 (not_295_out, B1);
  not not_296 (not_296_out, A2);
  not not_297 (not_297_out, B0);
  not not_298 (not_298_out, A2);
  not not_299 (not_299_out, D);
  not not_300 (not_300_out, B2);
  not not_301 (not_301_out, A2);
  not not_302 (not_302_out, A1);
  not not_303 (not_303_out, A0);
  not not_304 (not_304_out, D);
  not not_305 (not_305_out, B2);
  not not_306 (not_306_out, A1);
  not not_307 (not_307_out, D);
  not not_308 (not_308_out, B2);
  not not_309 (not_309_out, B0);
  not not_310 (not_310_out, B2);
  not not_311 (not_311_out, B1);
  not not_312 (not_312_out, B0);
  not not_313 (not_313_out, A1);
  not not_314 (not_314_out, A0);
  not not_315 (not_315_out, A1);
  not not_316 (not_316_out, A1);
  not not_317 (not_317_out, B2);
  not not_318 (not_318_out, B1);
  not not_319 (not_319_out, A1);
  not not_320 (not_320_out, A0);
  not not_321 (not_321_out, B2);
  not not_322 (not_322_out, B1);
  not not_323 (not_323_out, D);
  not not_324 (not_324_out, A0);
  not not_325 (not_325_out, B2);
  not not_326 (not_326_out, B0);
  not not_327 (not_327_out, D);
  not not_328 (not_328_out, B2);
  not not_329 (not_329_out, A1);
  not not_330 (not_330_out, A0);
  not not_331 (not_331_out, D);
  not not_332 (not_332_out, A1);
  not not_333 (not_333_out, B0);
  not not_334 (not_334_out, A1);
  not not_335 (not_335_out, A0);
  not not_336 (not_336_out, B1);
  not not_337 (not_337_out, A1);
  not not_338 (not_338_out, D);
  not not_339 (not_339_out, B1);
  not not_340 (not_340_out, A1);
  not not_341 (not_341_out, A0);
  not not_342 (not_342_out, D);
  not not_343 (not_343_out, B1);
  not not_344 (not_344_out, B1);
  not not_345 (not_345_out, B0);
  not not_346 (not_346_out, A0);
  not not_347 (not_347_out, D);
  not not_348 (not_348_out, B1);
  not not_349 (not_349_out, A0);
  not not_350 (not_350_out, B0);
  and and_1 (and_1_out, D, not_1_out, not_2_out, not_3_out, not_4_out);
  and and_2 (and_2_out, A0, not_5_out, B3, B2, B1, B0);
  and and_3 (and_3_out, A0, D, not_6_out, not_7_out, not_8_out);
  and and_4 (and_4_out, A1, not_9_out, B3, B2, B1);
  and and_5 (and_5_out, A1, D, not_10_out, not_11_out, not_12_out);
  and and_6 (and_6_out, A1, D, not_13_out, not_14_out, not_15_out);
  and and_7 (and_7_out, A1, A0, not_16_out, B3, B2, B0);
  and and_8 (and_8_out, A1, A0, D, not_17_out, not_18_out);
  and and_9 (and_9_out, A2, not_19_out, B3, B2);
  and and_10 (and_10_out, A2, D, not_20_out, not_21_out);
  and and_11 (and_11_out, A2, D, not_22_out, not_23_out, not_24_out);
  and and_12 (and_12_out, A2, A0, not_25_out, B3, B1, B0);
  and and_13 (and_13_out, A2, A0, D, not_26_out, not_27_out);
  and and_14 (and_14_out, A2, A1, not_28_out, B3, B1);
  and and_15 (and_15_out, A2, A1, D, not_29_out, not_30_out);
  and and_16 (and_16_out, A2, A1, D, not_31_out, not_32_out);
  and and_17 (and_17_out, A2, A1, A0, not_33_out, B3, B0);
  and and_18 (and_18_out, A2, A1, A0, D, not_34_out);
  and and_19 (and_19_out, A3, not_35_out, B3);
  and and_20 (and_20_out, A3, D, not_36_out);
  and and_21 (and_21_out, A3, D, not_37_out, not_38_out, not_39_out);
  and and_22 (and_22_out, A3, A0, not_40_out, B2, B1, B0);
  and and_23 (and_23_out, A3, A0, D, not_41_out, not_42_out);
  and and_24 (and_24_out, A3, A1, not_43_out, B2, B1);
  and and_25 (and_25_out, A3, A1, B3, not_44_out, not_45_out);
  and and_26 (and_26_out, A3, A1, D, not_46_out, not_47_out);
  and and_27 (and_27_out, A3, A1, A0, not_48_out, B2, B0);
  and and_28 (and_28_out, A3, A1, A0, B3, not_49_out);
  and and_29 (and_29_out, A3, A2, not_50_out, B2);
  and and_30 (and_30_out, A3, A2, B3, not_51_out);
  and and_31 (and_31_out, A3, A2, D, not_52_out, not_53_out);
  and and_32 (and_32_out, A3, A2, A0, not_54_out, B1, B0);
  and and_33 (and_33_out, A3, A2, A0, D, not_55_out);
  and and_34 (and_34_out, A3, A2, A1, not_56_out, B1);
  and and_35 (and_35_out, A3, A2, A1, B3, not_57_out);
  and and_36 (and_36_out, A3, A2, A1, D, not_58_out);
  and and_37 (and_37_out, A3, A2, A1, A0, B0);
  and and_38 (and_38_out, not_59_out, not_60_out, not_61_out, not_62_out, not_63_out, B3);
  and and_39 (and_39_out, not_64_out, not_65_out, not_66_out, not_67_out, B3, not_68_out);
  and and_40 (and_40_out, not_69_out, not_70_out, not_71_out, not_72_out, B3, not_73_out);
  and and_41 (and_41_out, not_74_out, not_75_out, not_76_out, not_77_out, B3, not_78_out);
  and and_42 (and_42_out, not_79_out, not_80_out, not_81_out, B3, not_82_out);
  and and_43 (and_43_out, not_83_out, not_84_out, not_85_out, B3, not_86_out, not_87_out);
  and and_44 (and_44_out, not_88_out, not_89_out, not_90_out, B3, not_91_out, not_92_out);
  and and_45 (and_45_out, not_93_out, B3, not_94_out, not_95_out, not_96_out);
  and and_46 (and_46_out, not_97_out, not_98_out, not_99_out, not_100_out, D, not_101_out, B0);
  and and_47 (and_47_out, not_102_out, not_103_out, not_104_out, D, not_105_out, B1);
  and and_48 (and_48_out, not_106_out, not_107_out, not_108_out, D, not_109_out, B1, B0);
  and and_49 (and_49_out, not_110_out, not_111_out, D, not_112_out, B2);
  and and_50 (and_50_out, not_113_out, not_114_out, not_115_out, D, not_116_out, B2, B0);
  and and_51 (and_51_out, not_117_out, not_118_out, D, not_119_out, B2, B1, B0);
  and and_52 (and_52_out, not_120_out, not_121_out, A0, not_122_out, B2, B1, B0);
  and and_53 (and_53_out, not_123_out, not_124_out, A0, B3, not_125_out, not_126_out);
  and and_54 (and_54_out, not_127_out, not_128_out, A1, not_129_out, B2, B1);
  and and_55 (and_55_out, not_130_out, not_131_out, A1, B3, not_132_out, not_133_out);
  and and_56 (and_56_out, not_134_out, A1, not_135_out, B3, not_136_out, not_137_out);
  and and_57 (and_57_out, not_138_out, not_139_out, A1, A0, not_140_out, B2, B0);
  and and_58 (and_58_out, not_141_out, not_142_out, A1, A0, B3, not_143_out);
  and and_59 (and_59_out, not_144_out, A2, not_145_out, not_146_out, B2);
  and and_60 (and_60_out, not_147_out, A2, not_148_out, not_149_out, B2, B1);
  and and_61 (and_61_out, not_150_out, A2, not_151_out, not_152_out, B3, not_153_out);
  and and_62 (and_62_out, not_154_out, A2, D, B3, not_155_out);
  and and_63 (and_63_out, not_156_out, A2, D, B3, not_157_out, not_158_out);
  and and_64 (and_64_out, not_159_out, A2, A0, not_160_out, not_161_out, B1, B0);
  and and_65 (and_65_out, not_162_out, A2, A0, D, B3, not_163_out);
  and and_66 (and_66_out, not_164_out, A2, A1, not_165_out, not_166_out, B1);
  and and_67 (and_67_out, not_167_out, A2, A1, D, B3, not_168_out);
  and and_68 (and_68_out, not_169_out, A2, A1, D, B3, not_170_out);
  and and_69 (and_69_out, not_171_out, A2, A1, A0, not_172_out, not_173_out, B0);
  and and_70 (and_70_out, not_174_out, A2, A1, A0, D, B3);
  and and_71 (and_71_out, A3, not_175_out, not_176_out, not_177_out, not_178_out, not_179_out);
  and and_72 (and_72_out, A3, not_180_out, not_181_out, not_182_out, not_183_out, not_184_out);
  and and_73 (and_73_out, A3, not_185_out, not_186_out, not_187_out, not_188_out, not_189_out);
  and and_74 (and_74_out, A3, not_190_out, not_191_out, not_192_out, not_193_out, not_194_out);
  and and_75 (and_75_out, A3, not_195_out, not_196_out, not_197_out, not_198_out);
  and and_76 (and_76_out, A3, not_199_out, not_200_out, not_201_out, not_202_out, not_203_out);
  and and_77 (and_77_out, A3, not_204_out, not_205_out, not_206_out, not_207_out, not_208_out);
  and and_78 (and_78_out, A3, not_209_out, not_210_out, not_211_out, not_212_out);
  and and_79 (and_79_out, A3, not_213_out, not_214_out, not_215_out, D, B3, B0);
  and and_80 (and_80_out, A3, not_216_out, not_217_out, D, B3, B1);
  and and_81 (and_81_out, A3, not_218_out, not_219_out, D, B3, B1, B0);
  and and_82 (and_82_out, A3, not_220_out, D, B3, B2);
  and and_83 (and_83_out, A3, not_221_out, D, B3, B2, B1);
  and and_84 (and_84_out, A3, not_222_out, A0, not_223_out, not_224_out, not_225_out);
  and and_85 (and_85_out, A3, not_226_out, A0, B3, B2, B1, B0);
  and and_86 (and_86_out, A3, not_227_out, A1, not_228_out, not_229_out, not_230_out);
  and and_87 (and_87_out, A3, A1, not_231_out, not_232_out, not_233_out, not_234_out);
  and and_88 (and_88_out, A3, not_235_out, A1, B3, B2, B1);
  and and_89 (and_89_out, A3, not_236_out, A1, A0, not_237_out, not_238_out);
  and and_90 (and_90_out, A3, not_239_out, A1, A0, B3, B2, B0);
  and and_91 (and_91_out, A3, A2, not_240_out, not_241_out, not_242_out, not_243_out);
  and and_92 (and_92_out, A3, A2, not_244_out, B3, B2);
  and and_93 (and_93_out, A3, A2, not_245_out, not_246_out, B3, B2, B0);
  and and_94 (and_94_out, A3, A2, not_247_out, B3, B2, B1, B0);
  and and_95 (and_95_out, A3, A2, D, not_248_out, not_249_out);
  and and_96 (and_96_out, A3, A2, D, not_250_out, not_251_out, not_252_out);
  and and_97 (and_97_out, A3, A2, A0, not_253_out, B3, B1, B0);
  and and_98 (and_98_out, A3, A2, A0, D, not_254_out, not_255_out);
  and and_99 (and_99_out, A3, A2, A1, not_256_out, B3, B1);
  and and_100 (and_100_out, A3, A2, A1, D, not_257_out, not_258_out);
  and and_101 (and_101_out, A3, A2, A1, D, not_259_out, not_260_out);
  and and_102 (and_102_out, A3, A2, A1, A0, not_261_out, B3, B0);
  and and_103 (and_103_out, A3, A2, A1, A0, D, not_262_out);
  and and_104 (and_104_out, not_263_out, not_264_out, not_265_out, not_266_out, B2);
  and and_105 (and_105_out, not_267_out, not_268_out, not_269_out, B2, not_270_out);
  and and_106 (and_106_out, not_271_out, B2, not_272_out, not_273_out);
  and and_107 (and_107_out, not_274_out, not_275_out, not_276_out, D, not_277_out, B0);
  and and_108 (and_108_out, not_278_out, not_279_out, D, not_280_out, B1);
  and and_109 (and_109_out, not_281_out, not_282_out, D, not_283_out, B1, B0);
  and and_110 (and_110_out, not_284_out, not_285_out, A0, not_286_out, B1, B0);
  and and_111 (and_111_out, not_287_out, not_288_out, A0, B2, not_289_out);
  and and_112 (and_112_out, not_290_out, A1, not_291_out, not_292_out, B1);
  and and_113 (and_113_out, not_293_out, A1, not_294_out, B2, not_295_out);
  and and_114 (and_114_out, not_296_out, A1, D, B2, not_297_out);
  and and_115 (and_115_out, not_298_out, A1, A0, not_299_out, not_300_out, B0);
  and and_116 (and_116_out, not_301_out, A1, A0, D, B2);
  and and_117 (and_117_out, A2, not_302_out, not_303_out, not_304_out, not_305_out);
  and and_118 (and_118_out, A2, not_306_out, not_307_out, not_308_out, not_309_out);
  and and_119 (and_119_out, A2, not_310_out, not_311_out, not_312_out);
  and and_120 (and_120_out, A2, not_313_out, not_314_out, D, B2, B0);
  and and_121 (and_121_out, A2, not_315_out, D, B2, B1);
  and and_122 (and_122_out, A2, not_316_out, A0, not_317_out, not_318_out);
  and and_123 (and_123_out, A2, not_319_out, A0, B2, B1, B0);
  and and_124 (and_124_out, A2, A1, not_320_out, not_321_out, not_322_out);
  and and_125 (and_125_out, A2, A1, not_323_out, B2, B1);
  and and_126 (and_126_out, A2, A1, not_324_out, B2, B1, B0);
  and and_127 (and_127_out, A2, A1, D, not_325_out, not_326_out);
  and and_128 (and_128_out, A2, A1, A0, not_327_out, B2, B0);
  and and_129 (and_129_out, A2, A1, A0, D, not_328_out);
  and and_130 (and_130_out, not_329_out, not_330_out, not_331_out, B1);
  and and_131 (and_131_out, not_332_out, B1, not_333_out);
  and and_132 (and_132_out, not_334_out, not_335_out, D, not_336_out, B0);
  and and_133 (and_133_out, not_337_out, A0, not_338_out, not_339_out, B0);
  and and_134 (and_134_out, not_340_out, A0, D, B1);
  and and_135 (and_135_out, A1, not_341_out, not_342_out, not_343_out);
  and and_136 (and_136_out, A1, not_344_out, not_345_out);
  and and_137 (and_137_out, A1, not_346_out, D, B1, B0);
  and and_138 (and_138_out, A1, A0, not_347_out, B1, B0);
  and and_139 (and_139_out, A1, A0, D, not_348_out);
  and and_140 (and_140_out, not_349_out, B0);
  and and_141 (and_141_out, A0, not_350_out);
  or or_1 (S1, and_130_out, and_131_out, and_132_out, and_133_out, and_134_out, and_135_out, and_136_out, and_137_out, and_138_out, and_139_out);
  or or_2 (S0, and_140_out, and_141_out);
  or or_3 (or_3_out, and_1_out, and_2_out, and_3_out, and_4_out, and_5_out, and_6_out, and_7_out, and_8_out, and_9_out, and_10_out, and_11_out, and_12_out, and_13_out, and_14_out, and_15_out, and_16_out, and_17_out, and_18_out, and_19_out);
  or or_4 (or_4_out, and_20_out, and_21_out, and_22_out, and_23_out, and_24_out, and_25_out, and_26_out, and_27_out, and_28_out, and_29_out, and_30_out, and_31_out, and_32_out, and_33_out, and_34_out, and_35_out, and_36_out, and_37_out);
  or or_5 (or_5_out, and_38_out, and_39_out, and_40_out, and_41_out, and_42_out, and_43_out, and_44_out, and_45_out, and_46_out, and_47_out, and_48_out, and_49_out, and_50_out, and_51_out, and_52_out, and_53_out, and_54_out, and_55_out, and_56_out, and_57_out, and_58_out, and_59_out);
  or or_6 (or_6_out, and_60_out, and_61_out, and_62_out, and_63_out, and_64_out, and_65_out, and_66_out, and_67_out, and_68_out, and_69_out, and_70_out, and_71_out, and_72_out, and_73_out, and_74_out, and_75_out, and_76_out, and_77_out, and_78_out, and_79_out, and_80_out, and_81_out);
  or or_7 (or_7_out, and_82_out, and_83_out, and_84_out, and_85_out, and_86_out, and_87_out, and_88_out, and_89_out, and_90_out, and_91_out, and_92_out, and_93_out, and_94_out, and_95_out, and_96_out, and_97_out, and_98_out, and_99_out, and_100_out, and_101_out, and_102_out, and_103_out);
  or or_8 (S32, and_104_out, and_105_out, and_106_out, and_107_out, and_108_out, and_109_out, and_110_out, and_111_out, and_112_out, and_113_out, and_114_out, and_115_out, and_116_out, and_117_out, and_118_out, and_119_out, and_120_out, and_121_out, and_122_out, and_123_out, and_124_out, and_125_out, and_126_out, and_127_out, and_128_out, and_129_out);
  or or_9 (C, or_3_out, or_4_out);
  or or_10 (S3, or_5_out, or_6_out, or_7_out);
endmodule

module CPU (
);

  wire register_1_p1, register_1_p2, register_1_p3, register_1_p4, register_1_p5, register_1_p6,
       register_1_p7, register_2_q0, register_2_q1, register_2_q2, register_2_q3, register_3_q0,
       register_3_q1, register_3_q2, undriven, undriven_2, undriven_3, undriven_4, undriven_5, undriven_6,
       undriven_7;

  // register register_1: pin names not known; wires that end beside it: register_1_p1, register_1_p2, register_1_p3, register_1_p4, register_1_p5, register_1_p6, register_1_p7
  register register_2 (
    .c(undriven_3), .d0(register_1_p2), .d1(register_1_p3), .d2(undriven), .d3(undriven_4),
    .q0(register_2_q0), .q1(register_2_q1), .q2(register_2_q2), .q3(register_2_q3));
  register register_3 (
    .c(undriven_7), .d0(undriven_2), .d1(undriven_5), .d2(undriven_6), .q0(register_3_q0),
    .q1(register_3_q1), .q2(register_3_q2));  // open: d3, q3
  ALU alu_1 (
    .A0(register_1_p4), .A1(register_1_p5), .A2(register_1_p6), .A3(register_1_p7), .B0(register_2_q0),
    .B1(register_2_q1), .B2(register_2_q2), .B3(register_2_q3), .I0(register_3_q0), .I1(register_3_q1),
    .I2(register_3_q2));  // open: D0, D1, D2, D3, C
endmodule
