// Logisim project cpu2.circ as structural Verilog
module adder (
  input  B,
  input  A,
  input  Cin,
  output Cout,
  output S
);

  wire and_1_out, and_2_out, xor_1_out;

  xor xor_1 (xor_1_out, A, B);
  and and_1 (and_1_out, A, B);
  xor xor_2 (S, xor_1_out, Cin);
  and and_2 (and_2_out, xor_1_out, Cin);
  or or_1 (Cout, and_2_out, and_1_out);
endmodule

module MUX (
  input  A,
  input  A_2,
  input  A_3,
  input  A_4,
  input  A_5,
  input  A_6,
  input  A_7,
  input  A_8,
  input  B,
  input  B_2,
  input  B_3,
  input  B_4,
  input  B_5,
  input  B_6,
  input  B_7,
  input  B_8,
  input  S,
  output C,
  output C_2,
  output C_3,
  output C_4,
  output C_5,
  output C_6,
  output C_7,
  output C_8
);

  Multiplexer #(.enable("false")) multiplexer_1 (.in0(A), .in1(B), .out(C), .sel(S));
  Multiplexer #(.enable("false")) multiplexer_2 (.in0(A_2), .in1(B_2), .out(C_2), .sel(S));
  Multiplexer #(.enable("false")) multiplexer_3 (.in0(A_3), .in1(B_3), .out(C_3), .sel(S));
  Multiplexer #(.enable("false")) multiplexer_4 (.in0(A_4), .in1(B_4), .out(C_4), .sel(S));
  Multiplexer #(.enable("false")) multiplexer_5 (.in0(A_6), .in1(B_6), .out(C_6), .sel(S));
  Multiplexer #(.enable("false")) multiplexer_6 (.in0(A_5), .in1(B_5), .out(C_5), .sel(S));
  Multiplexer #(.enable("false")) multiplexer_7 (.in0(A_7), .in1(B_7), .out(C_7), .sel(S));
  Multiplexer #(.enable("false")) multiplexer_8 (.in0(A_8), .in1(B_8), .out(C_8), .sel(S));
endmodule

module add_sub (
  input  [7:0] in_1,
  input  [7:0] in_2,
  input  in_3,
  output out_4,
  output [7:0] out_5
);

  wire adder_1_cout, adder_2_cout, adder_3_cout, adder_4_cout, adder_5_cout, adder_6_cout, adder_7_cout,
       adder_8_cout, xor_1_out, xor_3_out, xor_4_out, xor_5_out, xor_6_out, xor_7_out, xor_8_out, xor_9_out;

  xor xor_1 (xor_1_out, in_1[7], in_3);
  adder adder_1 (.Cout(adder_1_cout), .B(xor_1_out), .A(in_2[7]), .S(out_5[7]), .Cin(adder_2_cout));
  xor xor_2 (out_4, adder_1_cout, adder_2_cout);
  xor xor_3 (xor_3_out, in_1[6], in_3);
  adder adder_2 (.Cout(adder_2_cout), .B(xor_3_out), .A(in_2[6]), .S(out_5[6]), .Cin(adder_3_cout));
  xor xor_4 (xor_4_out, in_1[5], in_3);
  xor xor_5 (xor_5_out, in_1[4], in_3);
  adder adder_3 (.Cout(adder_3_cout), .B(xor_4_out), .A(in_2[5]), .S(out_5[5]), .Cin(adder_4_cout));
  xor xor_6 (xor_6_out, in_1[3], in_3);
  adder adder_4 (.Cout(adder_4_cout), .B(xor_5_out), .A(in_2[4]), .S(out_5[4]), .Cin(adder_5_cout));
  adder adder_5 (.Cout(adder_5_cout), .B(xor_6_out), .A(in_2[3]), .S(out_5[3]), .Cin(adder_6_cout));
  xor xor_7 (xor_7_out, in_1[2], in_3);
  adder adder_6 (.Cout(adder_6_cout), .B(xor_7_out), .A(in_2[2]), .S(out_5[2]), .Cin(adder_7_cout));
  xor xor_8 (xor_8_out, in_1[0], in_3);
  xor xor_9 (xor_9_out, in_1[1], in_3);
  adder adder_7 (.Cout(adder_7_cout), .B(xor_9_out), .A(in_2[1]), .S(out_5[1]), .Cin(adder_8_cout));
  adder adder_8 (.Cout(adder_8_cout), .B(xor_8_out), .A(in_2[0]), .S(out_5[0]), .Cin(in_3));
endmodule

module ALU (
  input  [7:0] in_1,
  input  [7:0] in_2,
  input  in_3,
  input  in_4,
  output [7:0] out_5
);

  wire [7:0] add_sub_1_out_5, and_1_out, multiplexer_2_out, or_1_out;

  add_sub add_sub_1 (.in_3(in_3), .in_1(in_1), .in_2(in_2), .out_5(add_sub_1_out_5));  // open: out_4
  Multiplexer #(.width(8), .enable("false")) multiplexer_1 (
    .in0(add_sub_1_out_5), .in1(multiplexer_2_out), .out(out_5), .sel(in_4));
  assign and_1_out = in_1 & in_2;  // AND_Gate and_1, 8 bits wide
  Multiplexer #(.width(8), .enable("false")) multiplexer_2 (
    .in0(and_1_out), .in1(or_1_out), .out(multiplexer_2_out), .sel(in_3));
  assign or_1_out = in_1 | in_2;  // OR_Gate or_1, 8 bits wide
endmodule
